// Logisim project 数逻实验三.circ as structural Verilog: 6 circuits, main circuit 键盘输入部分
module \键盘输入部分  (
  input  \开始读出 
);

  wire and_1_out, and_2_out, CIK, d_ff_1_q, d_ff_2_q, d_ff_2_qn, keyboard_1_avail, Q, re, Ta, Tb, Tc,
       \有限机部分_1_c0 , \有限机部分_1_c1 ;
  wire [6:0] keyboard_1_data;

  Keyboard keyboard_1 (.clk(and_1_out), .clr(re), .avail(keyboard_1_avail), .data(keyboard_1_data));  // open: re
  and and_1 (and_1_out, CIK, \开始读出 );
  Button \u_清零  (.out(re));
  LED led_1 (.in(keyboard_1_avail));
  Comparator #(.width(7)) comparator_1 (.a(keyboard_1_data), .b(7'b1001010), .eq(Ta));  // open: gt, lt
  Comparator #(.width(7)) comparator_2 (.a(keyboard_1_data), .b(7'b1001101), .eq(Tb));  // open: gt, lt
  Comparator #(.width(7)) comparator_3 (.a(keyboard_1_data), .b(7'b1010101), .eq(Tc));  // open: gt, lt
  Clock clock_1 (.out(CIK));
  \有限机部分  \u_有限机部分_1  (.S1(d_ff_1_q), .S0(d_ff_2_q), .Ta(Ta), .Tb(Tb), .Tc(Tc), .C1(\有限机部分_1_c1 ), .C0(\有限机部分_1_c0 ));
  and and_2 (and_2_out, CIK, \开始读出 );
  TTY #(.rows(1), .cols(1)) tty_1 (.data(7'b1010110), .clk(Q), .clr(re));  // open: we
  D_Flip_Flop d_ff_1 (.clk(and_2_out), .D(\有限机部分_1_c1 ), .Q(d_ff_1_q));  // open: Qn, preset, en, reset
  D_Flip_Flop d_ff_2 (.clk(and_2_out), .D(\有限机部分_1_c0 ), .Q(d_ff_2_q), .Qn(d_ff_2_qn));  // open: preset, en, reset
  and and_3 (Q, d_ff_1_q, d_ff_2_q);

  // Other names for the same wires on the sheet: s = \开始读出 
endmodule

module \有限机部分  (
  input  S1,
  input  S0,
  input  Ta,
  input  Tb,
  input  Tc,
  output C1,
  output C0
);

  wire and_1_out, and_2_out, and_3_out, and_4_out, not_1_out, not_2_out, not_3_out, not_4_out, not_5_out;

  not not_1 (not_1_out, S1);
  not not_2 (not_2_out, S0);
  not not_3 (not_3_out, S1);
  not not_4 (not_4_out, S0);
  not not_5 (not_5_out, S0);
  and and_1 (and_1_out, not_1_out, S0, Tb);
  and and_2 (and_2_out, S1, not_2_out, Tc);
  and and_3 (and_3_out, not_3_out, not_4_out, Ta);
  and and_4 (and_4_out, S1, not_5_out, Tc);
  or or_1 (C1, and_1_out, and_2_out);
  or or_2 (C0, and_3_out, and_4_out);
endmodule

module \应用部分_1_0  (
  input  _5,
  input  _10,
  input  _25,
  input  in_4,
  output [7:0] out_5
);

  wire comparator_1_eq, comparator_1_lt, or_2_out;
  wire [7:0] adder_1_out, multiplexer_1_out, multiplexer_2_out, multiplexer_3_out, multiplexer_4_out,
       multiplexer_5_out, or_1_out, Q;

  Multiplexer #(.width(8), .enable("false")) multiplexer_1 (
    .in0({8{1'b0}}), .in1(8'h5), .out(multiplexer_1_out), .sel(_5));
  Multiplexer #(.width(8), .enable("false")) multiplexer_2 (
    .in0({8{1'b0}}), .in1(8'h10), .out(multiplexer_2_out), .sel(_10));
  Multiplexer #(.width(8), .enable("false")) multiplexer_3 (
    .in0({8{1'b0}}), .in1(8'h25), .out(multiplexer_3_out), .sel(_25));
  assign or_1_out = multiplexer_1_out | multiplexer_2_out | multiplexer_3_out;  // OR_Gate or_1, 8 bits wide
  Multiplexer #(.width(8), .enable("false")) multiplexer_4 (
    .in0(Q), .in1({8{1'b0}}), .out(multiplexer_4_out), .sel(or_2_out));
  Adder adder_1 (.a(multiplexer_4_out), .b(or_1_out), .out(adder_1_out));  // open: cin, cout
  Register register_1 (.D(adder_1_out), .Q(Q), .clk(in_4));  // open: en, clr
  Comparator #(.mode("unsigned")) comparator_1 (
    .a(8'h25), .b(Q), .eq(comparator_1_eq), .lt(comparator_1_lt));  // open: gt
  or or_2 (or_2_out, comparator_1_eq, comparator_1_lt);
  Multiplexer #(.width(8), .enable("false")) multiplexer_5 (
    .in0({8{1'b0}}), .in1(8'h25), .out(multiplexer_5_out), .sel(or_2_out));
  Subtractor subtractor_1 (.a(Q), .b(multiplexer_5_out), .out(out_5));  // open: bin, bout
endmodule

module \有限机部分2_0  (
  input  s2,
  input  s1,
  input  s0,
  input  a,
  input  b,
  input  c,
  output c2,
  output c1,
  output c0
);

  wire and_1_out, and_2_out, and_3_out, and_4_out, and_5_out, and_6_out, and_7_out, and_8_out, and_9_out,
       and_10_out, and_11_out, and_12_out, and_13_out, and_14_out, and_15_out, not_1_out, not_2_out,
       not_3_out, not_4_out, not_5_out, not_6_out, not_7_out, not_8_out, not_9_out, not_10_out, not_11_out,
       not_12_out, not_13_out, not_14_out, not_15_out, not_16_out, not_17_out, not_18_out, not_19_out,
       not_20_out, not_21_out, not_22_out, not_23_out, not_24_out, not_25_out, not_26_out, not_27_out,
       not_28_out, not_29_out, not_30_out, or_1_out, or_2_out, or_3_out, or_4_out, or_5_out, or_6_out,
       or_7_out;

  not not_1 (not_1_out, s2);
  not not_2 (not_2_out, s1);
  not not_3 (not_3_out, s0);
  not not_4 (not_4_out, s2);
  not not_5 (not_5_out, s1);
  not not_6 (not_6_out, s2);
  not not_7 (not_7_out, s0);
  or or_1 (or_1_out, b, c);
  not not_8 (not_8_out, s2);
  or or_2 (or_2_out, a, b, c);
  not not_9 (not_9_out, s1);
  not not_10 (not_10_out, s0);
  or or_3 (or_3_out, a, b, c);
  not not_11 (not_11_out, s2);
  not not_12 (not_12_out, s1);
  not not_13 (not_13_out, s0);
  not not_14 (not_14_out, s2);
  not not_15 (not_15_out, s1);
  or or_4 (or_4_out, a, b, c);
  not not_16 (not_16_out, s2);
  not not_17 (not_17_out, s0);
  or or_5 (or_5_out, c, a);
  not not_18 (not_18_out, s2);
  not not_19 (not_19_out, s1);
  not not_20 (not_20_out, s0);
  or or_6 (or_6_out, b, c);
  not not_21 (not_21_out, s2);
  not not_22 (not_22_out, s1);
  not not_23 (not_23_out, s0);
  or or_7 (or_7_out, a, c);
  not not_24 (not_24_out, s2);
  not not_25 (not_25_out, s1);
  not not_26 (not_26_out, s2);
  not not_27 (not_27_out, s0);
  not not_28 (not_28_out, s2);
  not not_29 (not_29_out, s1);
  not not_30 (not_30_out, s0);
  and and_1 (and_1_out, not_1_out, not_2_out, not_3_out, c);
  and and_2 (and_2_out, not_4_out, not_5_out, s0, c);
  and and_3 (and_3_out, not_6_out, s1, not_7_out, or_1_out);
  and and_4 (and_4_out, not_8_out, s1, s0, or_2_out);
  and and_5 (and_5_out, s2, not_9_out, not_10_out, or_3_out);
  and and_6 (and_6_out, not_11_out, not_12_out, not_13_out, b);
  and and_7 (and_7_out, not_14_out, not_15_out, s0, or_4_out);
  and and_8 (and_8_out, not_16_out, s1, not_17_out, or_5_out);
  and and_9 (and_9_out, not_18_out, s1, s0, c);
  and and_10 (and_10_out, s2, not_19_out, not_20_out, or_6_out);
  and and_11 (and_11_out, not_21_out, not_22_out, not_23_out, or_7_out);
  and and_12 (and_12_out, not_24_out, not_25_out, s0, b);
  and and_13 (and_13_out, not_26_out, s1, not_27_out, a);
  and and_14 (and_14_out, not_28_out, s1, s0, b);
  and and_15 (and_15_out, s2, not_29_out, not_30_out, a);
  or or_8 (c2, and_1_out, and_2_out, and_3_out, and_4_out, and_5_out);
  or or_9 (c1, and_6_out, and_7_out, and_8_out, and_9_out, and_10_out);
  or or_10 (c0, and_11_out, and_12_out, and_13_out, and_14_out, and_15_out);
endmodule

// 5
module \应用部分2_0  (
  output [7:0] out_1
);

  wire _5, _10, _25, clock_1_out, comparator_1_eq, comparator_1_gt, not_1_out, or_1_out, or_3_out, RE, s0,
       s1, s2, \应用输出_1_q , \有限机部分2_0_1_c0 , \有限机部分2_0_1_c1 , \有限机部分2_0_1_c2 ;
  wire [7:0] adder_1_out, multiplexer_1_out, multiplexer_2_out, multiplexer_3_out, multiplexer_4_out,
       or_2_out, Q, subtractor_1_out;

  Button u__5 (.out(_5));
  Button u__10 (.out(_10));
  Button u__25 (.out(_25));
  Button \u_取出汽水_找出余额  (.out(RE));
  or or_1 (or_1_out, RE, _5, _10, _25);
  \有限机部分2_0  \u_有限机部分2_0_1  (
    .s2(s2), .s1(s1), .s0(s0), .a(_5), .b(_10), .c(_25), .c2(\有限机部分2_0_1_c2 ), .c1(\有限机部分2_0_1_c1 ),
    .c0(\有限机部分2_0_1_c0 ));
  not not_1 (not_1_out, or_1_out);
  Multiplexer #(.width(8), .enable("false")) multiplexer_1 (
    .in0({8{1'b0}}), .in1(8'h5), .out(multiplexer_1_out), .sel(_5));
  Multiplexer #(.width(8), .enable("false")) multiplexer_2 (
    .in0({8{1'b0}}), .in1(8'h10), .out(multiplexer_2_out), .sel(_10));
  Multiplexer #(.width(8), .enable("false")) multiplexer_3 (
    .in0({8{1'b0}}), .in1(8'h25), .out(multiplexer_3_out), .sel(_25));
  D_Flip_Flop d_ff_1 (.clk(not_1_out), .D(\有限机部分2_0_1_c2 ), .Q(s2));  // open: Qn, preset, en, reset
  D_Flip_Flop d_ff_2 (.clk(not_1_out), .D(\有限机部分2_0_1_c1 ), .Q(s1));  // open: Qn, preset, en, reset
  D_Flip_Flop d_ff_3 (.clk(not_1_out), .D(\有限机部分2_0_1_c0 ), .Q(s0));  // open: Qn, preset, en, reset
  assign or_2_out = multiplexer_1_out | multiplexer_2_out | multiplexer_3_out;  // OR_Gate or_2, 8 bits wide
  Adder adder_1 (.a(Q), .b(or_2_out), .out(adder_1_out));  // open: cin, cout
  Clock clock_1 (.out(clock_1_out));
  Hex_Digit_Display hex_digit_display_1 (.value(out_1[7:4]));  // open: dp
  Register register_1 (.D(adder_1_out), .Q(Q), .clk(clock_1_out), .clr(RE));  // open: en
  LED led_1 (.in(\应用输出_1_q ));
  \应用输出  \u_应用输出_1  (.s2(s2), .s1(s1), .s0(s0), .q(\应用输出_1_q ));
  Hex_Digit_Display hex_digit_display_2 (.value(out_1[3:0]));  // open: dp
  Comparator comparator_1 (.a(Q), .b(8'h25), .gt(comparator_1_gt), .eq(comparator_1_eq));  // open: lt
  or or_3 (or_3_out, comparator_1_gt, comparator_1_eq);
  Multiplexer #(.width(8), .enable("false")) multiplexer_4 (
    .in0({8{1'b0}}), .in1(8'h25), .out(multiplexer_4_out), .sel(or_3_out));
  Subtractor subtractor_1 (.a(Q), .b(multiplexer_4_out), .out(subtractor_1_out));  // open: bin, bout
  Register register_2 (.D(subtractor_1_out), .Q(out_1), .clk(clock_1_out));  // open: en, clr

  // Other names for the same wires on the sheet: 余额[7:0] = out_1

  // Notes on the sheet:
  //   当前余额
endmodule

module \应用输出  (
  input  s2,
  input  s1,
  input  s0,
  output q
);

  wire and_1_out, and_2_out, not_1_out, not_2_out;

  not not_1 (not_1_out, s1);
  not not_2 (not_2_out, s0);
  and and_1 (and_1_out, s2, not_1_out, s0);
  and and_2 (and_2_out, s2, s1, not_2_out);
  or or_1 (q, and_1_out, and_2_out);
endmodule
