// Logisim project 数逻实验二.circ as structural Verilog: 11 circuits, main circuit 4比特寄存器
module \_4比特寄存器  (
  input  [3:0] in_1,
  input  \时钟 ,
  output [3:0] out_3
);

  \D触发器  \d触发器_1  (.D(in_1[0]), .C(\时钟 ), .Q(out_3[0]));  // open: nQ
  \D触发器  \d触发器_2  (.D(in_1[1]), .C(\时钟 ), .Q(out_3[1]));  // open: nQ
  \D触发器  \d触发器_3  (.D(in_1[2]), .C(\时钟 ), .Q(out_3[2]));  // open: nQ
  \D触发器  \d触发器_4  (.D(in_1[3]), .C(\时钟 ), .Q(out_3[3]));  // open: nQ
endmodule

module \SR锁存器  (
  input  RS,
  input  S,
  output Q,
  output nQ
);

  nor nor_1 (Q, RS, nQ);
  nor nor_2 (nQ, Q, S);
endmodule

module \D锁存器  (
  input  D,
  input  C,
  output Q,
  output nQ
);

  wire and_1_out, and_2_out, not_1_out;

  not not_1 (not_1_out, D);
  and and_1 (and_1_out, C, not_1_out);
  and and_2 (and_2_out, C, D);
  \SR锁存器  \sr锁存器_1  (.RS(and_1_out), .S(and_2_out), .Q(Q), .nQ(nQ));
endmodule

module \D触发器  (
  input  D,
  input  C,
  output Q,
  output nQ
);

  wire \d锁存器_1_q , not_1_out;

  not not_1 (not_1_out, C);
  \D锁存器  \d锁存器_1  (.D(D), .C(not_1_out), .Q(\d锁存器_1_q ));  // open: nQ
  \D锁存器  \d锁存器_2  (.D(\d锁存器_1_q ), .C(C), .Q(Q), .nQ(nQ));
endmodule

module \二进制正计时器  (
  input  \开启始终为0 
);

  wire clock_1_out, comparator_1_eq, or_1_out;
  wire [3:0] adder_1_out, multiplexer_1_out, \n4比特寄存器_1_out_3 ;

  Adder #(.width(4)) adder_1 (.a(\n4比特寄存器_1_out_3 ), .b(4'b0001), .out(adder_1_out));  // open: cin, cout
  Comparator #(.width(4)) comparator_1 (.a(\n4比特寄存器_1_out_3 ), .b(4'b1001), .eq(comparator_1_eq));  // open: gt, lt
  Multiplexer #(.width(4), .enable("false")) multiplexer_1 (
    .in0(adder_1_out), .in1(4'b0000), .out(multiplexer_1_out), .sel(or_1_out));
  or or_1 (or_1_out, comparator_1_eq, \开启始终为0 );
  \_4比特寄存器  \u_4比特寄存器_1  (.in_1(multiplexer_1_out), .\时钟 (clock_1_out), .out_3(\n4比特寄存器_1_out_3 ));
  Clock clock_1 (.out(clock_1_out));
  Hex_Digit_Display hex_digit_display_1 (.value(\n4比特寄存器_1_out_3 ));  // open: dp
endmodule

module \走马灯  (
  input  \不同预设 ,
  input  \开启预设 
);

  wire clock_1_out, comparator_1_eq, \d触发器_1_q , \d触发器_2_q , \d触发器_3_q , \d触发器_4_q , \d触发器_5_q , \d触发器_6_q ,
       \d触发器_7_q , \d触发器_8_q , \d触发器_9_q , multiplexer_2_out, multiplexer_3_out, multiplexer_4_out,
       multiplexer_5_out, or_1_out, \重置_out ;
  wire [3:0] adder_1_out, multiplexer_1_out, \n4比特寄存器_1_out_3 ;

  Adder #(.width(4)) adder_1 (.a(\n4比特寄存器_1_out_3 ), .b(4'b0001), .out(adder_1_out));  // open: cin, cout
  Comparator #(.width(4)) comparator_1 (.a(\n4比特寄存器_1_out_3 ), .b(4'b0011), .eq(comparator_1_eq));  // open: gt, lt
  Button \u_重置  (.out(\重置_out ));
  Multiplexer #(.width(4), .enable("false")) multiplexer_1 (
    .in0(adder_1_out), .in1(4'b0000), .out(multiplexer_1_out), .sel(or_1_out));
  or or_1 (or_1_out, comparator_1_eq, \重置_out );
  \_4比特寄存器  \u_4比特寄存器_1  (.in_1(multiplexer_1_out), .\时钟 (clock_1_out), .out_3(\n4比特寄存器_1_out_3 ));
  Multiplexer #(.enable("false")) multiplexer_2 (.in0(1'b0), .in1(\d触发器_4_q ), .out(multiplexer_2_out), .sel(\开启预设 ));
  Clock #(.highDuration(2), .lowDuration(2)) clock_1 (.out(clock_1_out));
  Multiplexer #(.select(2), .enable("false")) multiplexer_3 (
    .in0(1'b0), .in1(1'b1), .in2(1'b0), .in3(1'b1), .out(multiplexer_3_out), .sel(\n4比特寄存器_1_out_3 [1:0]));
  Multiplexer #(.select(2), .enable("false")) multiplexer_4 (
    .in0(1'b1), .in1(1'b1), .in2(1'b0), .in3(1'b0), .out(multiplexer_4_out), .sel(\n4比特寄存器_1_out_3 [1:0]));
  LED led_1 (.in(\d触发器_1_q ));
  \D触发器  \d触发器_1  (.D(multiplexer_2_out), .C(clock_1_out), .Q(\d触发器_1_q ));  // open: nQ
  Multiplexer #(.enable("false")) multiplexer_5 (
    .in0(multiplexer_3_out), .in1(multiplexer_4_out), .out(multiplexer_5_out), .sel(\不同预设 ));
  LED led_2 (.in(\d触发器_2_q ));
  \D触发器  \d触发器_2  (.D(\d触发器_1_q ), .C(clock_1_out), .Q(\d触发器_2_q ));  // open: nQ
  \D触发器  \d触发器_3  (.D(\d触发器_2_q ), .C(clock_1_out), .Q(\d触发器_3_q ));  // open: nQ
  \D触发器  \d触发器_4  (.D(multiplexer_5_out), .C(clock_1_out), .Q(\d触发器_4_q ));  // open: nQ
  LED led_3 (.in(\d触发器_3_q ));
  LED led_4 (.in(\d触发器_5_q ));
  \D触发器  \d触发器_5  (.D(\d触发器_3_q ), .C(clock_1_out), .Q(\d触发器_5_q ));  // open: nQ
  LED led_5 (.in(\d触发器_6_q ));
  \D触发器  \d触发器_6  (.D(\d触发器_5_q ), .C(clock_1_out), .Q(\d触发器_6_q ));  // open: nQ
  LED led_6 (.in(\d触发器_7_q ));
  \D触发器  \d触发器_7  (.D(\d触发器_6_q ), .C(clock_1_out), .Q(\d触发器_7_q ));  // open: nQ
  \D触发器  \d触发器_8  (.D(\d触发器_7_q ), .C(clock_1_out), .Q(\d触发器_8_q ));  // open: nQ
  LED led_7 (.in(\d触发器_8_q ));
  LED led_8 (.in(\d触发器_9_q ));
  \D触发器  \d触发器_9  (.D(\d触发器_8_q ), .C(clock_1_out), .Q(\d触发器_9_q ));  // open: nQ
endmodule

module \点阵灯  (
  input  \修改参数 ,
  input  [3:0] \初始化数据 
);

  wire and_1_out, clock_1_out;
  wire [1:0] counter_1_q;
  wire [3:0] controlled_buffer_1_out, demultiplexer_1_out0, demultiplexer_1_out1, demultiplexer_1_out2,
       demultiplexer_1_out3, \n4_4存储矩阵_1_out_4 ;

  Counter #(.width(2), .max('h3)) counter_1 (.Q(counter_1_q), .clk(clock_1_out));  // open: load, D, count, carry, clr
  and and_1 (and_1_out, clock_1_out, \修改参数 );
  Clock clock_1 (.out(clock_1_out));
  \_4_4存储矩阵  \u_4_4存储矩阵_1  (
    .\地址 (counter_1_q), .\时钟 (and_1_out), .\写入 (controlled_buffer_1_out), .out_4(\n4_4存储矩阵_1_out_4 ));
  DotMatrix #(.matrixcols(4), .matrixrows(4)) dotmatrix_1 (
    .col0(demultiplexer_1_out0), .col1(demultiplexer_1_out1), .col2(demultiplexer_1_out2),
    .col3(demultiplexer_1_out3));
  assign controlled_buffer_1_out = \修改参数  ? \初始化数据  : 4'bz;  // Controlled_Buffer controlled_buffer_1
  Demultiplexer #(.select(2), .width(4), .enable("false")) demultiplexer_1 (
    .out0(demultiplexer_1_out0), .out1(demultiplexer_1_out1), .out2(demultiplexer_1_out2),
    .out3(demultiplexer_1_out3), .in(\n4_4存储矩阵_1_out_4 ), .sel(counter_1_q));
endmodule

module \_4_4存储矩阵  (
  input  [1:0] \地址 ,
  input  \时钟 ,
  input  [3:0] \写入 ,
  output [3:0] out_4
);

  wire \n2_4译码器_1_b0 , \n2_4译码器_1_b1 , \n2_4译码器_1_b2 , \n2_4译码器_1_b3 ;

  \_2_4译码器  \u_2_4译码器_1  (
    .A1(\地址 [1]), .A0(\地址 [0]), .b0(\n2_4译码器_1_b0 ), .b1(\n2_4译码器_1_b1 ), .b2(\n2_4译码器_1_b2 ),
    .b3(\n2_4译码器_1_b3 ));
  \使能D触发器  \u_使能d触发器_1  (.CLK(\时钟 ), .EN(\n2_4译码器_1_b0 ), .D(\写入 [0]), .Q(out_4[0]));  // open: nQ
  \使能D触发器  \u_使能d触发器_2  (.CLK(\时钟 ), .EN(\n2_4译码器_1_b1 ), .D(\写入 [0]), .Q(out_4[0]));  // open: nQ
  \使能D触发器  \u_使能d触发器_3  (.CLK(\时钟 ), .EN(\n2_4译码器_1_b2 ), .D(\写入 [0]), .Q(out_4[0]));  // open: nQ
  \使能D触发器  \u_使能d触发器_4  (.CLK(\时钟 ), .EN(\n2_4译码器_1_b3 ), .D(\写入 [0]), .Q(out_4[0]));  // open: nQ
  \使能D触发器  \u_使能d触发器_5  (.CLK(\时钟 ), .EN(\n2_4译码器_1_b0 ), .D(\写入 [1]), .Q(out_4[1]));  // open: nQ
  \使能D触发器  \u_使能d触发器_6  (.CLK(\时钟 ), .EN(\n2_4译码器_1_b1 ), .D(\写入 [1]), .Q(out_4[1]));  // open: nQ
  \使能D触发器  \u_使能d触发器_7  (.CLK(\时钟 ), .EN(\n2_4译码器_1_b2 ), .D(\写入 [1]), .Q(out_4[1]));  // open: nQ
  \使能D触发器  \u_使能d触发器_8  (.CLK(\时钟 ), .EN(\n2_4译码器_1_b3 ), .D(\写入 [1]), .Q(out_4[1]));  // open: nQ
  \使能D触发器  \u_使能d触发器_9  (.CLK(\时钟 ), .EN(\n2_4译码器_1_b0 ), .D(\写入 [2]), .Q(out_4[2]));  // open: nQ
  \使能D触发器  \u_使能d触发器_10  (.CLK(\时钟 ), .EN(\n2_4译码器_1_b1 ), .D(\写入 [2]), .Q(out_4[2]));  // open: nQ
  \使能D触发器  \u_使能d触发器_11  (.CLK(\时钟 ), .EN(\n2_4译码器_1_b2 ), .D(\写入 [2]), .Q(out_4[2]));  // open: nQ
  \使能D触发器  \u_使能d触发器_12  (.CLK(\时钟 ), .EN(\n2_4译码器_1_b3 ), .D(\写入 [2]), .Q(out_4[2]));  // open: nQ
  \使能D触发器  \u_使能d触发器_13  (.CLK(\时钟 ), .EN(\n2_4译码器_1_b0 ), .D(\写入 [3]), .Q(out_4[3]));  // open: nQ
  \使能D触发器  \u_使能d触发器_14  (.CLK(\时钟 ), .EN(\n2_4译码器_1_b1 ), .D(\写入 [3]), .Q(out_4[3]));  // open: nQ
  \使能D触发器  \u_使能d触发器_15  (.CLK(\时钟 ), .EN(\n2_4译码器_1_b2 ), .D(\写入 [3]), .Q(out_4[3]));  // open: nQ
  \使能D触发器  \u_使能d触发器_16  (.CLK(\时钟 ), .EN(\n2_4译码器_1_b3 ), .D(\写入 [3]), .Q(out_4[3]));  // open: nQ
endmodule

module \使能D触发器  (
  input  CLK,
  input  EN,
  input  D,
  output Q,
  output nQ
);

  wire \d触发器_1_nq , \d触发器_1_q , multiplexer_1_out;

  Multiplexer #(.enable("false")) multiplexer_1 (.in0(\d触发器_1_q ), .in1(D), .out(multiplexer_1_out), .sel(EN));
  \D触发器  \d触发器_1  (.D(multiplexer_1_out), .C(CLK), .Q(\d触发器_1_q ), .nQ(\d触发器_1_nq ));
  assign Q = EN ? \d触发器_1_q  : 1'bz;  // Controlled_Buffer controlled_buffer_1
  assign nQ = EN ? \d触发器_1_nq  : 1'bz;  // Controlled_Buffer controlled_buffer_2
endmodule

module \_2_4译码器  (
  input  A1,
  input  A0,
  output b0,
  output b1,
  output b2,
  output b3
);

  wire not_1_out, not_2_out, not_3_out, not_4_out;

  not not_1 (not_1_out, A0);
  not not_2 (not_2_out, A1);
  not not_3 (not_3_out, A1);
  not not_4 (not_4_out, A0);
  and and_1 (b3, A1, A0);
  and and_2 (b0, not_1_out, not_2_out);
  and and_3 (b1, not_3_out, A0);
  and and_4 (b2, A1, not_4_out);
endmodule

module \类烟花  (
  output [12:0] out_1
);

  wire clock_1_out;
  wire [1:0] counter_1_q;
  wire [12:0] rom_1_data, rom_2_data, rom_3_data, rom_4_data, rom_5_data, rom_6_data, rom_7_data, rom_8_data,
       rom_9_data, rom_10_data, rom_11_data, rom_13_data;

  Counter #(.width(2), .max('h3)) counter_1 (.Q(counter_1_q), .clk(clock_1_out));  // open: load, D, count, carry, clr
  ROM #(.addrWidth(2), .dataWidth(13)) rom_1 (.addr(counter_1_q), .data(rom_1_data));  // open: sel
  ROM #(.addrWidth(2), .dataWidth(13)) rom_2 (.addr(counter_1_q), .data(rom_2_data));  // open: sel
  ROM #(.addrWidth(2), .dataWidth(13)) rom_3 (.addr(counter_1_q), .data(rom_3_data));  // open: sel
  ROM #(.addrWidth(2), .dataWidth(13)) rom_4 (.addr(counter_1_q), .data(rom_4_data));  // open: sel
  ROM #(.addrWidth(2), .dataWidth(13)) rom_5 (.addr(counter_1_q), .data(rom_5_data));  // open: sel
  ROM #(.addrWidth(2), .dataWidth(13)) rom_6 (.addr(counter_1_q), .data(rom_6_data));  // open: sel
  ROM #(.addrWidth(2), .dataWidth(13)) rom_7 (.addr(counter_1_q), .data(rom_7_data));  // open: sel
  Clock clock_1 (.out(clock_1_out));
  ROM #(.addrWidth(2), .dataWidth(13)) rom_8 (.addr(counter_1_q), .data(rom_8_data));  // open: sel
  ROM #(.addrWidth(2), .dataWidth(13)) rom_9 (.addr(counter_1_q), .data(rom_9_data));  // open: sel
  ROM #(.addrWidth(2), .dataWidth(13)) rom_10 (.addr(counter_1_q), .data(rom_10_data));  // open: sel
  ROM #(.addrWidth(2), .dataWidth(13)) rom_11 (.addr(counter_1_q), .data(rom_11_data));  // open: sel
  ROM #(.addrWidth(2), .dataWidth(13)) rom_12 (.addr(counter_1_q), .data(out_1));  // open: sel
  DotMatrix #(.inputtype("row"), .matrixcols(13), .matrixrows(13)) dotmatrix_1 (
    .row0(rom_1_data), .row1(rom_3_data), .row2(rom_6_data), .row3(rom_8_data), .row4(rom_10_data),
    .row5(out_1), .row6(rom_4_data), .row7(rom_2_data), .row8(rom_5_data), .row9(rom_7_data),
    .row10(rom_9_data), .row11(rom_11_data), .row12(rom_13_data));
  ROM #(.addrWidth(2), .dataWidth(13)) rom_13 (.addr(counter_1_q), .data(rom_13_data));  // open: sel

  // Notes on the sheet:
  //   contents of rom_1 (hex, n*v repeats v):
  //   0 0 0 40
  //   contents of rom_2 (hex, n*v repeats v):
  //   0 120 250
  //   contents of rom_3 (hex, n*v repeats v):
  //   0 0 0 248
  //   contents of rom_4 (hex, n*v repeats v):
  //   40 110 404 1001
  //   contents of rom_5 (hex, n*v repeats v):
  //   0 40 0 254
  //   contents of rom_6 (hex, n*v repeats v):
  //   0 0 40 834
  //   contents of rom_7 (hex, n*v repeats v):
  //   0 0 40 1428
  //   contents of rom_8 (hex, n*v repeats v):
  //   0 0 0 342
  //   contents of rom_9 (hex, n*v repeats v):
  //   0 0 0 865
  //   contents of rom_10 (hex, n*v repeats v):
  //   0 40 0 424
  //   contents of rom_11 (hex, n*v repeats v):
  //   0 0 0 1428
  //   contents of rom_12 (hex, n*v repeats v):
  //   0 120 290 248
  //   contents of rom_13 (hex, n*v repeats v):
  //   0 0 0 40
endmodule
