// Logisim project lec1-冯诺依曼模型与指令集_Rev0.1.circ as structural Verilog
module \摄氏_华氏温度转换_专用设计  (
);

  wire clock_1_out;
  wire [7:0] adder_1_out, divider_1_out, multiplier_1_out, temp_C_q;

  Register temp_C (.Q(temp_C_q), .clk(clock_1_out));  // open: D, en, clr
  Clock clock_1 (.out(clock_1_out));
  Multiplier multiplier_1 (.a(temp_C_q), .b(8'h9), .out(multiplier_1_out));  // open: cin, cout
  Divider divider_1 (.a(multiplier_1_out), .b(8'h5), .out(divider_1_out));  // open: upper, rem
  Adder adder_1 (.a(divider_1_out), .b(8'h20), .out(adder_1_out));  // open: cin, cout
  Register temp_F (.D(adder_1_out), .clk(clock_1_out));  // open: en, Q, clr

  // Notes on the sheet:
  //   以摄氏转华氏为例
endmodule

module \_2_2矩阵乘法阵列  (
);

  wire CLK;
  wire [0:0] \地址计数器_q ;
  wire [7:0] register_1_q, rom_1_data, rom_2_data, \乘累加运算单元_1_乘累加结果 , \乘累加运算单元_1_输入a寄存值 , \乘累加运算单元_2_乘累加结果 ,
       \乘累加运算单元_3_乘累加结果 , \乘累加运算单元_3_输入a寄存值 , \乘累加运算单元_4_乘累加结果 ;

  Clock clock_1 (.out(CLK));
  // Probe on {1'b0, \地址计数器_q [0]}
  Counter #(.width(1), .max('h1), .ongoal("stay")) \u_地址计数器  (
    .Q(\地址计数器_q [0]), .clk(CLK));  // open: load, D, count, carry, clr
  ROM #(.addrWidth(2)) rom_1 (.addr({1'b0, \地址计数器_q [0]}), .data(rom_1_data));  // open: sel
  // Probe on rom_1_data
  \乘累加运算单元  \u_乘累加运算单元_1  (
    .CLK(CLK), .A(rom_1_data), .B(8'h4), .\相邻列累加输入 ({8{1'b0}}), .\输入A寄存值 (\乘累加运算单元_1_输入a寄存值 ),
    .\乘累加结果 (\乘累加运算单元_1_乘累加结果 ));
  // Probe on \乘累加运算单元_1_输入a寄存值 
  \乘累加运算单元  \u_乘累加运算单元_2  (
    .CLK(CLK), .A(\乘累加运算单元_1_输入a寄存值 ), .B(8'h5), .\相邻列累加输入 ({8{1'b0}}), .\乘累加结果 (\乘累加运算单元_2_乘累加结果 ));  // open: 输入A寄存值
  // Probe on \乘累加运算单元_1_乘累加结果 
  // Probe on \乘累加运算单元_2_乘累加结果 
  ROM #(.addrWidth(2)) rom_2 (.addr({1'b0, \地址计数器_q [0]}), .data(rom_2_data));  // open: sel
  // Probe on \乘累加运算单元_3_输入a寄存值 
  Register register_1 (.D(rom_2_data), .Q(register_1_q), .clk(CLK));  // open: en, clr
  // Probe on register_1_q
  \乘累加运算单元  \u_乘累加运算单元_3  (
    .CLK(CLK), .A(register_1_q), .B(8'h6), .\相邻列累加输入 (\乘累加运算单元_1_乘累加结果 ), .\输入A寄存值 (\乘累加运算单元_3_输入a寄存值 ),
    .\乘累加结果 (\乘累加运算单元_3_乘累加结果 ));
  // Probe on \乘累加运算单元_3_乘累加结果 
  \乘累加运算单元  \u_乘累加运算单元_4  (
    .CLK(CLK), .A(\乘累加运算单元_3_输入a寄存值 ), .B(8'h7), .\相邻列累加输入 (\乘累加运算单元_2_乘累加结果 ), .\乘累加结果 (\乘累加运算单元_4_乘累加结果 ));  // open: 输入A寄存值
  // Probe on \乘累加运算单元_4_乘累加结果 

  // Notes on the sheet:
  //   矩阵B元素
  //   以下数字电路展示一种2×2矩阵乘法的设计
  //   矩阵A第一列
  //   contents of rom_1 (hex, n*v repeats v):
  //   2 1 3 4
  //   操作方式：在模拟状态下单击时钟并产生上升沿，通过上升沿触发地址计数器的值发生改变，从而输入矩阵A
  //   矩阵A第二列
  //   contents of rom_2 (hex, n*v repeats v):
  //   1 3 3 4
  //   使用寄存器延迟一拍
  //   矩阵C计算结果
endmodule

module \乘累加运算单元  (
  input  CLK,
  input  [7:0] A,
  input  [7:0] B,
  input  [7:0] \相邻列累加输入 ,
  output [7:0] \乘累加结果 ,
  output [7:0] \输入A寄存值 
);

  wire [7:0] adder_1_out, multiplier_1_out;

  Multiplier multiplier_1 (.a(A), .b(B), .out(multiplier_1_out));  // open: cin, cout
  Register \u_输入A寄存  (.D(A), .Q(\输入A寄存值 ), .clk(CLK));  // open: en, clr
  // Probe on adder_1_out
  Adder adder_1 (.a(multiplier_1_out), .b(\相邻列累加输入 ), .out(adder_1_out));  // open: cin, cout
  Register \u_乘积并累加结果寄存  (.D(adder_1_out), .Q(\乘累加结果 ), .clk(CLK));  // open: en, clr
endmodule

module \摄氏_华氏温度转换_冯氏模型v1  (
  input  [1:0] \控制存储器的地址 ,
  input  [1:0] \控制复用器的选择信号 
);

  wire clock_1_out;
  wire [7:0] adder_1_out, divider_1_out, multiplexer_1_out, multiplier_1_out, ram_1_data;

  Clock clock_1 (.out(clock_1_out));
  // Probe on ram_1_data
  RAM #(.addrWidth(2), .bus("separate")) ram_1 (
    .addr(\控制存储器的地址 ), .din(multiplexer_1_out), .data(ram_1_data), .str(1'b1), .clk(clock_1_out));  // open: sel, ld, clr
  Multiplier multiplier_1 (.a(ram_1_data), .b(8'h9), .out(multiplier_1_out));  // open: cin, cout
  Divider divider_1 (.a(ram_1_data), .b(8'h5), .out(divider_1_out));  // open: upper, rem
  Adder adder_1 (.a(ram_1_data), .b(8'h20), .out(adder_1_out));  // open: cin, cout
  Multiplexer #(.select(2), .width(8), .enable("false")) multiplexer_1 (
    .in0(multiplier_1_out), .in1(divider_1_out), .in2(adder_1_out), .out(multiplexer_1_out),
    .sel(\控制复用器的选择信号 ));  // open: in3
  // Probe on multiplexer_1_out

  // Notes on the sheet:
  //   存储器
  //   选择信号等于0：乘以9
  //   选择信号等于1：除以5
  //   选择信号等于2：加32
endmodule

module \摄氏_华氏温度转换_冯氏模型v2  (
  input  in_1
);

  wire CLK, undriven, \程序计数器_carry ;
  wire [1:0] \程序计数器_q ;
  wire [3:0] rom_1_data;
  wire [7:0] adder_1_out, divider_1_out, multiplexer_1_out, multiplier_1_out, ram_1_data;

  Counter #(.width(2), .max('h2)) \u_程序计数器  (
    .Q(\程序计数器_q ), .carry(\程序计数器_carry ), .clk(CLK));  // open: load, D, count, clr
  Clock clock_1 (.out(CLK));
  ROM #(.addrWidth(2), .dataWidth(4)) rom_1 (.addr(\程序计数器_q ), .data(rom_1_data));  // open: sel
  // Probe on ram_1_data
  RAM #(.addrWidth(2), .bus("separate")) ram_1 (
    .addr(rom_1_data[3:2]), .din(multiplexer_1_out), .data(ram_1_data), .str(1'b1), .clk(CLK), .clr(undriven));  // open: sel, ld
  Multiplier multiplier_1 (.a(ram_1_data), .b(8'h9), .out(multiplier_1_out));  // open: cin, cout
  Divider divider_1 (.a(ram_1_data), .b(8'h5), .out(divider_1_out));  // open: upper, rem
  Adder adder_1 (.a(ram_1_data), .b(8'h20), .out(adder_1_out));  // open: cin, cout
  Multiplexer #(.select(2), .width(8), .enable("false")) multiplexer_1 (
    .in0(multiplier_1_out), .in1(divider_1_out), .in2(adder_1_out), .out(multiplexer_1_out),
    .sel(rom_1_data[1:0]));  // open: in3
  // Probe on multiplexer_1_out

  // Notes on the sheet:
  //   指令存储器
  //   数据存储器
  //   contents of rom_1 (hex, n*v repeats v):
  //   0 1 2
  //   低两位存放选择信号信息
  //   高两位存放选择数据存储器地址信息
  //   选择信号等于0：乘以9
  //   选择信号等于1：除以5
  //   选择信号等于2：加32
endmodule
