// Logisim project MIPS-CPU-Design-framework—课设.circ as structural Verilog: 4 circuits, main circuit main
// 10signed
module main (
);

  wire ALUSrc, and_2_out, and_3_out, BEQCOO, Button, CLK, clock_1_out, clock_2_out, clock_3_out, Coin,
       comparator_1_eq, comparator_2_eq, comparator_3_eq, comparator_4_eq, comparator_5_eq, comparator_6_eq,
       comparator_7_eq, comparator_8_eq, comparator_9_eq, comparator_10_eq, comparator_11_eq,
       controlled_inverter_1_out, Equ, JUMP, JUMP_r, MemtoReg, MemtoReg_r, MemWrite, MemWrite_r, not_1_out,
       not_3_out, or_1_out, or_3_out, or_4_out, or_5_out, or_6_out, or_7_out, or_8_out, PCSrc, PCSrc_r,
       RegDst, RegWrite, RegWrite_r, Return, RST, START, T1, T2, T3, T4, T5, Taken, \数据冒险 ;
  wire [3:0] ALUOp, ALUOp_r;
  wire [4:0] W__r, W_num;
  wire [9:0] Fanal_Result, multiplexer_6_out, Result;
  wire [25:0] shifter_1_out;
  wire [31:0] adder_2_out, adder_3_out, alu_1_result, ALU_X, ALU_X_r, ALU_Y, ALU_Y_r, \beq或bne跳转 ,
       bit_extender_1_out, bit_extender_2_out, CoinAdd, DATA, DATA_r, Fanal_Data, inStruction, inStruction_r,
       \J指令跳转 , Last, main_1_reg1, main_1_reg2_2, multiplexer_1_out, multiplexer_4_out, multiplexer_5_out,
       multiplexer_13_out, New_inS, Old_inS, PC_1, PC_1_r, ram_1_data, register_1_q, register_2_q,
       register_3_q, register_4_q, register_5_q, register_6_q, rom_1_data, shifter_2_out, SPC, SPC_R,
       SPC_r_t, \立即数 , \立即数_r ;

  // Probe on New_inS
  Register #(.width(32)) PC (.D(New_inS), .Q(SPC), .clk(or_1_out), .clr(RST));  // open: en
  or or_1 (or_1_out, Coin, clock_1_out);
  Clock clock_1 (.out(clock_1_out));
  Button \u_总复位  (.out(RST));
  Adder #(.width(32)) adder_1 (.a(32'h4), .b(SPC), .out(Last));  // open: cin, cout
  // Probe on \beq或bne跳转 
  Multiplier #(.width(32)) multiplier_1 (.a(\立即数_r ), .b(32'h4), .out(\beq或bne跳转 ));  // open: cin, cout
  and and_1 (BEQCOO, PCSrc_r, Equ);
  Clock clock_2 (.out(clock_2_out));
  or or_2 (Taken, JUMP_r, BEQCOO);
  buf or_3 (or_3_out, Coin);  // OR_Gate
  not not_1 (not_1_out, or_3_out);
  buf or_4 (or_4_out, clock_2_out);  // OR_Gate
  ROM #(.addrWidth(12), .dataWidth(32)) rom_1 (.addr(SPC[13:2]), .data(rom_1_data));  // open: sel
  // Probe on rom_1_data
  not not_2 (CLK, controlled_inverter_1_out);
  assign controlled_inverter_1_out = not_1_out ? ~or_4_out : 1'bz;  // Controlled_Inverter controlled_inverter_1
  IF_ID if_id_1 (
    .SPC(SPC), .PC_1(Last), .Instruction(rom_1_data), .SPC_r(SPC_R), .PC_1_r(PC_1),
    .Instruction_r(inStruction), .Bubble(Taken), .CLK(CLK), .\清空 (RST));  // open: 暂停
  // Probe on inStruction
  Shifter #(.width(26)) shifter_1 (.in(inStruction_r[25:0]), .\dist (5'b00010), .out(shifter_1_out));
  assign bit_extender_1_out = {{28{1'b0}}, SPC_r_t[31:28]};  // Bit_Extender bit_extender_1
  assign bit_extender_2_out = {{6{1'b0}}, shifter_1_out};  // Bit_Extender bit_extender_2
  Shifter #(.width(32)) shifter_2 (.in(bit_extender_1_out), .\dist (5'b11100), .out(shifter_2_out));
  // Probe on \J指令跳转 
  Adder #(.width(32)) adder_2 (.a(bit_extender_2_out), .b(shifter_2_out), .out(adder_2_out));  // open: cin, cout
  Register #(.width(32)) register_1 (.D(Last), .Q(register_1_q), .clk(Button));  // open: en, clr
  Comparator #(.width(32)) comparator_1 (.a(Old_inS), .b(32'hfc), .eq(comparator_1_eq));  // open: gt, lt
  // Probe on inStruction[20:16]
  // Probe on inStruction[15:0]
  Subtractor #(.width(32)) subtractor_1 (.a(adder_2_out), .b(32'h3000), .out(\J指令跳转 ));  // open: bin, bout
  Multiplexer #(.width(32), .enable("false")) multiplexer_1 (
    .in0(Old_inS), .in1(32'h124), .out(multiplexer_1_out), .sel(Button));
  Adder #(.width(32)) adder_3 (.a(PC_1_r), .b(\beq或bne跳转 ), .out(adder_3_out));  // open: cin, cout
  // Probe on inStruction[25:21]
  Multiplexer #(.width(5), .enable("false")) multiplexer_2 (
    .in0(inStruction[20:16]), .in1(inStruction[15:11]), .out(W_num), .sel(RegDst));
  Multiplexer #(.width(32), .enable("false")) multiplexer_3 (
    .in0(multiplexer_1_out), .in1(register_1_q), .out(New_inS), .sel(comparator_1_eq));
  // Probe on W_num
  assign \立即数  = {{16{inStruction[15]}}, inStruction[15:0]};  // Bit_Extender bit_extender_3
  Multiplexer #(.width(32), .enable("false")) multiplexer_4 (
    .in0(DATA_r), .in1(32'h1), .out(multiplexer_4_out), .sel(Button));
  // Probe on Last
  Multiplexer #(.width(32), .enable("false")) multiplexer_5 (
    .in0(Last), .in1(adder_3_out), .out(multiplexer_5_out), .sel(BEQCOO));
  \regfile参考设计_main  main_1 (
    .Reg1_num(inStruction[25:21]), .Reg2(inStruction[20:16]), .Write_Reg_num(W__r), .Din(multiplexer_13_out),
    .Write_Enable(RegWrite_r), .Clock(CLK), .Reg1(main_1_reg1), .Reg2_2(main_1_reg2_2));  // open: s0_Value, s1_Value, s2_Value, ra_Value
  Comparator #(.width(5)) comparator_2 (.a(W__r), .b(inStruction[20:16]), .eq(comparator_2_eq));  // open: gt, lt
  Multiplexer #(.width(10), .enable("false")) multiplexer_6 (
    .in0(Result), .in1({10{1'b0}}), .out(multiplexer_6_out), .sel(Button));
  Multiplexer #(.width(32), .enable("false")) multiplexer_7 (
    .in0(multiplexer_4_out), .in1(CoinAdd), .out(Fanal_Data), .sel(Coin));
  Comparator #(.width(5)) comparator_3 (.a(W__r), .b(inStruction[25:21]), .eq(comparator_3_eq));  // open: gt, lt
  and and_2 (and_2_out, comparator_3_eq, \数据冒险 );
  and and_3 (and_3_out, comparator_2_eq, \数据冒险 );
  Multiplexer #(.width(10), .enable("false")) multiplexer_8 (
    .in0(multiplexer_6_out), .in1(10'h5), .out(Fanal_Result), .sel(Coin));
  Multiplexer #(.width(32), .enable("false")) multiplexer_9 (
    .in0(multiplexer_5_out), .in1(\J指令跳转 ), .out(Old_inS), .sel(JUMP_r));
  Multiplexer #(.width(32), .enable("false")) multiplexer_10 (
    .in0(main_1_reg1), .in1(multiplexer_13_out), .out(ALU_X), .sel(and_2_out));
  Multiplexer #(.width(32), .enable("false")) multiplexer_11 (
    .in0(main_1_reg2_2), .in1(multiplexer_13_out), .out(DATA), .sel(and_3_out));
  Multiplexer #(.width(32), .enable("false")) multiplexer_12 (.in0(DATA), .in1(\立即数 ), .out(ALU_Y), .sel(ALUSrc));
  // Probe on Fanal_Data
  Register #(.width(32)) register_2 (.D(Fanal_Data), .Q(register_2_q), .clk(T1));  // open: en, clr
  Register #(.width(32)) register_3 (.D(Fanal_Data), .Q(register_3_q), .clk(T2));  // open: en, clr
  Register #(.width(32)) register_4 (.D(Fanal_Data), .Q(register_4_q), .clk(T3));  // open: en, clr
  Register #(.width(32)) register_5 (.D(Fanal_Data), .Q(register_5_q), .clk(T5));  // open: en, clr
  Register #(.width(32)) register_6 (.D(Fanal_Data), .Q(register_6_q), .clk(T4));  // open: en, clr
  // Probe on DATA
  ALU alu_1 (
    .AluOP(ALUOp_r), .X(ALU_X_r), .Equal(Equ), .Result({alu_1_result[31:12], Result, alu_1_result[1:0]}),
    .Y(ALU_Y_r));  // open: Signed_Overflow, Result_2, UnSigned_Overflow
  ID_EX id_ex_1 (
    .SRC(SPC_R), .PC_1(PC_1), .PCSrc(PCSrc), .\立即数 (\立即数 ), .Instruction(inStruction), .W_num(W_num),
    .ALU_X(ALU_X), .ALU_Y(ALU_Y), .MemData(DATA), .ALUOp(ALUOp), .MemWrite(MemWrite), .MemtoReg(MemtoReg),
    .RegWrite(RegWrite), .Jump(JUMP), .SRC_r(SPC_r_t), .PC_1_r(PC_1_r), .PCSrc_r(PCSrc_r), .\立即数_r (\立即数_r ),
    .Instruction_r(inStruction_r), .W__r(W__r), .ALU_X_r(ALU_X_r), .ALU_Y_r(ALU_Y_r), .MemData_r(DATA_r),
    .ALUOp_r(ALUOp_r), .MemWrite_r(MemWrite_r), .MemtoReg_r(MemtoReg_r), .RegWrite_r(RegWrite_r),
    .Jump_r(JUMP_r), .\清空 (Taken), .CLK(CLK), .RST(RST));
  Hex_Digit_Display hex_digit_display_1 (.value(register_2_q[3:0]));  // open: dp
  Hex_Digit_Display hex_digit_display_2 (.value(register_3_q[3:0]));  // open: dp
  Hex_Digit_Display hex_digit_display_3 (.value(register_5_q[3:0]));  // open: dp
  // Probe on W__r
  Hex_Digit_Display hex_digit_display_4 (.value(register_4_q[3:0]));  // open: dp
  Hex_Digit_Display hex_digit_display_5 (.value(register_6_q[3:0]));  // open: dp
  Button button_1 (.out(Button));
  \控制器  \u_控制器_1  (
    .ALU_OP(ALUOp), .OP(inStruction[31:26]), .RegDst(RegDst), .RegWrite(RegWrite), .MemToReg(MemtoReg),
    .MemWrite(MemWrite), .AluSrc(ALUSrc), .Func(inStruction[5:0]), .PCSRC(PCSrc), .JUMP(JUMP));
  LED led_1 (.in(START));
  Button button_2 (.out(Coin));
  or or_5 (or_5_out, MemWrite_r, Coin, Button);
  RAM #(.addrWidth(10), .dataWidth(32), .bus("separate")) ram_1 (
    .addr(Fanal_Result), .din(Fanal_Data), .data(ram_1_data), .str(or_5_out), .clk(clock_3_out));  // open: sel, ld, clr
  Clock clock_3 (.out(clock_3_out));
  Comparator #(.width(5)) comparator_4 (.a(inStruction[25:21]), .b(W__r), .eq(comparator_4_eq));  // open: gt, lt
  Comparator #(.width(5)) comparator_5 (.a(inStruction[20:16]), .b(W__r), .eq(comparator_5_eq));  // open: gt, lt
  Comparator #(.width(5)) comparator_6 (.a({5{1'b0}}), .b(W__r), .eq(comparator_6_eq));  // open: gt, lt
  or or_6 (or_6_out, comparator_4_eq, comparator_5_eq);
  not not_3 (not_3_out, comparator_6_eq);
  Multiplexer #(.width(32), .enable("false")) multiplexer_13 (
    .in0({alu_1_result[31:12], Result, alu_1_result[1:0]}), .in1(ram_1_data), .out(multiplexer_13_out),
    .sel(MemtoReg_r));
  Counter #(.width(32), .max('hffffffff)) counter_1 (
    .load(Button), .D(CoinAdd), .Q(CoinAdd), .clk(or_7_out), .clr(Return));  // open: count, carry
  or or_7 (or_7_out, Coin, Button);
  and and_4 (\数据冒险 , or_6_out, not_3_out, RegWrite_r);
  // Probe on Fanal_Result
  Comparator #(.width(10)) comparator_7 (.a(Fanal_Result), .b(10'h1), .eq(comparator_7_eq));  // open: gt, lt
  Comparator #(.width(10)) comparator_8 (.a(Fanal_Result), .b(10'h2), .eq(comparator_8_eq));  // open: gt, lt
  Comparator #(.width(10)) comparator_9 (.a(Fanal_Result), .b(10'h3), .eq(comparator_9_eq));  // open: gt, lt
  Comparator #(.width(10)) comparator_10 (.a(Fanal_Result), .b(10'h6), .eq(comparator_10_eq));  // open: gt, lt
  Comparator #(.width(10)) comparator_11 (.a(Fanal_Result), .b(10'h5), .eq(comparator_11_eq));  // open: gt, lt
  LED led_2 (.in(\数据冒险 ));
  and and_5 (T1, MemWrite_r, comparator_7_eq);
  and and_6 (T2, MemWrite_r, comparator_8_eq);
  and and_7 (T3, MemWrite_r, comparator_9_eq);
  and and_8 (T4, MemWrite_r, comparator_10_eq);
  Comparator #(.width(32)) comparator_12 (.a(CoinAdd), .b({32{1'b0}}), .gt(START), .lt(Return));  // open: eq
  or or_8 (or_8_out, MemWrite_r, Coin);
  and and_9 (T5, or_8_out, comparator_11_eq);

  // Other names for the same wires on the sheet: HAO[9:0] = Fanal_Result; R2_num[4:0] = inStruction[20:16];
  //   R1_num[4:0] = inStruction[25:21]; MenRes[31:0] = Fanal_Data

  // Notes on the sheet:
  //   复位
  //   时钟
  //   程序计数器
  //   PC+1
  //   指令存储器
  //   contents of rom_1 (hex, n*v repeats v):
  //   20040000 20050004 20060008 2007000c 200d0010 22100001 22310009 21290001 216b0001 0 0 aca90000
  //   aceb0000 0 0 214a0001 216b0001 0 0 acca0000 aceb0000 0 0 214a0001 216b0001 0 0 aceb0000 acca0000 0 0
  //   131082a 1020001f 151082a 10200020 171082a 10200021 8000c07 ac800000 8db80004 310082a 10200001
  //   8000c3f 2318ffff adb80004 8ca90000 8cca0000 8ceb0000 112a0003 114b0002 112b0001 8000c3f 8dae0008
  //   21ce0001 adae0008 114b0001 8000c3f 11490001 8000c3f 8dae0008 21ce0001 adae0008 8000c3f 8000c1f
  //   20090000 aca90000 8000c21 200a0000 acca0000 8000c23 200b0000 aceb0000 8000c07 8c8c0000 0 1190ffda
  //   8000c3f
  //   外部信号
  //   IF/ID
  //   指令译码
  //   指令字
  //   rs
  //   rt
  //   rd
  //   Imm16
  //   数据通路
  //   中断服务
  //   注：Equ表示x==y的结果
  //   按键映射内存地址
  //   ID/EX
  //   控制器
  //   当前币数
  //   当前得分
  //   游玩按钮
  //   投币按钮
  //   亮起表示游戏可玩
  //   数据存储器
  //   Coin添加
  //   数字冒险
  //   数码管读取更新
endmodule

module \控制器  (
  input  [5:0] OP,
  input  [5:0] Func,
  output RegDst,
  output RegWrite,
  output MemToReg,
  output MemWrite,
  output AluSrc,
  output PCSRC,
  output JUMP,
  output [3:0] ALU_OP
);

  wire ADD, ADDI, BEQ, comparator_3_eq, comparator_7_eq, comparator_8_eq, comparator_10_eq, comparator_11_eq,
       MUL, NOP, R, SLT;
  wire [3:0] multiplexer_1_out;

  Comparator #(.width(6)) comparator_1 (.a(OP), .b(6'b001000), .eq(ADDI));  // open: gt, lt
  Comparator #(.width(6)) comparator_2 (.a(OP), .b(6'b101011), .eq(MemWrite));  // open: gt, lt
  Comparator #(.width(6)) comparator_3 (.a(OP), .b(6'b011100), .eq(comparator_3_eq));  // open: gt, lt
  Comparator #(.width(6)) comparator_4 (.a(OP), .b(6'b100011), .eq(MemToReg));  // open: gt, lt
  Comparator #(.width(6)) comparator_5 (.a(OP), .b(6'b000010), .eq(JUMP));  // open: gt, lt
  Comparator #(.width(6)) comparator_6 (.a(OP), .b(6'b000100), .eq(BEQ));  // open: gt, lt
  or or_1 (RegDst, MUL, SLT, R, ADD);
  or or_2 (RegWrite, ADDI, MemToReg, R, SLT, ADD, MUL);
  Comparator #(.width(6)) comparator_7 (.a(Func), .b(6'b000010), .eq(comparator_7_eq));  // open: gt, lt
  Comparator #(.width(6)) comparator_8 (.a(Func), .b(6'b101010), .eq(comparator_8_eq));  // open: gt, lt
  Comparator #(.width(6)) comparator_9 (.a(OP), .b({6{1'b0}}), .eq(R));  // open: gt, lt
  Comparator #(.width(6)) comparator_10 (.a(Func), .b({6{1'b0}}), .eq(comparator_10_eq));  // open: gt, lt
  Comparator #(.width(6)) comparator_11 (.a(Func), .b(6'b100000), .eq(comparator_11_eq));  // open: gt, lt
  and and_1 (MUL, comparator_3_eq, comparator_7_eq);
  and and_2 (SLT, comparator_8_eq, R);
  and and_3 (NOP, R, comparator_10_eq);
  and and_4 (ADD, R, comparator_11_eq);
  or or_3 (AluSrc, ADDI, MemToReg, MemWrite);
  or or_4 (PCSRC, JUMP, BEQ);
  Multiplexer #(.width(4), .enable("false")) multiplexer_1 (
    .in0(4'b0101), .in1(4'b0011), .out(multiplexer_1_out), .sel(MUL));
  Multiplexer #(.width(4), .enable("false")) multiplexer_2 (
    .in0(multiplexer_1_out), .in1(4'b1011), .out(ALU_OP), .sel(SLT));

  // Other names for the same wires on the sheet: J = JUMP; LW = MemToReg; SW = MemWrite

  // Notes on the sheet:
  //   指令译码信号
  //   指令译码逻辑
  //   ADDI指令：OP=8
  //   SW指令：OP=0x2b
  //   MUL指令：OP=0x1C, Func=2
  //   根据MIPS指令集架构定义(具体查阅教材附录A.10.3)
  //   ALU控制器逻辑
  //   根据此工程的ALU设计，ALU_OP=5 时执行加法，ALU_OP=3时执行乘法
endmodule

module IF_ID (
  input  [31:0] SPC,
  input  [31:0] PC_1,
  input  [31:0] Instruction,
  input  \暂停 ,
  input  Bubble,
  input  CLK,
  input  \清空 ,
  output [31:0] SPC_r,
  output [31:0] PC_1_r,
  output [31:0] Instruction_r
);

  wire not_1_out;
  wire [31:0] multiplexer_1_out;

  not not_1 (not_1_out, \暂停 );
  Multiplexer #(.width(32), .enable("false")) multiplexer_1 (
    .in0(Instruction), .in1({32{1'b0}}), .out(multiplexer_1_out), .sel(Bubble));
  Register #(.width(32)) register_1 (.en(not_1_out), .Q(SPC_r), .clk(CLK), .clr(\清空 ));  // open: D
  Register #(.width(32)) register_2 (.D(PC_1), .en(not_1_out), .Q(PC_1_r), .clk(CLK), .clr(\清空 ));
  Register #(.width(32)) register_3 (.D(multiplexer_1_out), .en(not_1_out), .Q(Instruction_r), .clk(CLK), .clr(\清空 ));
endmodule

module ID_EX (
  input  [31:0] SRC,
  input  [31:0] PC_1,
  input  PCSrc,
  input  [31:0] \立即数 ,
  input  [31:0] Instruction,
  input  [4:0] W_num,
  input  [31:0] ALU_X,
  input  [31:0] ALU_Y,
  input  [31:0] MemData,
  input  [3:0] ALUOp,
  input  MemWrite,
  input  MemtoReg,
  input  RegWrite,
  input  Jump,
  input  \清空 ,
  input  CLK,
  input  RST,
  output [31:0] SRC_r,
  output [31:0] PC_1_r,
  output PCSrc_r,
  output [31:0] \立即数_r ,
  output [31:0] Instruction_r,
  output [4:0] W__r,
  output [31:0] ALU_X_r,
  output [31:0] ALU_Y_r,
  output [31:0] MemData_r,
  output [3:0] ALUOp_r,
  output MemWrite_r,
  output MemtoReg_r,
  output RegWrite_r,
  output Jump_r
);

  wire multiplexer_1_out, multiplexer_9_out, multiplexer_10_out, multiplexer_11_out, multiplexer_12_out;
  wire [3:0] multiplexer_8_out;
  wire [4:0] multiplexer_4_out;
  wire [31:0] multiplexer_2_out, multiplexer_3_out, multiplexer_5_out, multiplexer_6_out, multiplexer_7_out;

  Multiplexer #(.enable("false")) multiplexer_1 (.in0(PCSrc), .in1(1'b0), .out(multiplexer_1_out), .sel(\清空 ));
  Multiplexer #(.width(32), .enable("false")) multiplexer_2 (
    .in0(\立即数 ), .in1({32{1'b0}}), .out(multiplexer_2_out), .sel(\清空 ));
  Multiplexer #(.width(32), .enable("false")) multiplexer_3 (
    .in0(Instruction), .in1({32{1'b0}}), .out(multiplexer_3_out), .sel(\清空 ));
  Multiplexer #(.width(5), .enable("false")) multiplexer_4 (
    .in0(W_num), .in1({5{1'b0}}), .out(multiplexer_4_out), .sel(\清空 ));
  Multiplexer #(.width(32), .enable("false")) multiplexer_5 (
    .in0(ALU_X), .in1({32{1'b0}}), .out(multiplexer_5_out), .sel(\清空 ));
  Multiplexer #(.width(32), .enable("false")) multiplexer_6 (
    .in0(ALU_Y), .in1({32{1'b0}}), .out(multiplexer_6_out), .sel(\清空 ));
  Multiplexer #(.width(32), .enable("false")) multiplexer_7 (
    .in0(MemData), .in1({32{1'b0}}), .out(multiplexer_7_out), .sel(\清空 ));
  Multiplexer #(.width(4), .enable("false")) multiplexer_8 (
    .in0(ALUOp), .in1(4'b0000), .out(multiplexer_8_out), .sel(\清空 ));
  Multiplexer #(.enable("false")) multiplexer_9 (.in0(MemWrite), .in1(1'b0), .out(multiplexer_9_out), .sel(\清空 ));
  Multiplexer #(.enable("false")) multiplexer_10 (.in0(MemtoReg), .in1(1'b0), .out(multiplexer_10_out), .sel(\清空 ));
  Multiplexer #(.enable("false")) multiplexer_11 (.in0(RegWrite), .in1(1'b0), .out(multiplexer_11_out), .sel(\清空 ));
  Multiplexer #(.enable("false")) multiplexer_12 (.in0(Jump), .in1(1'b0), .out(multiplexer_12_out), .sel(\清空 ));
  Pull_Resistor pull_resistor_1 (.node(\清空 ));
  Register #(.width(32)) register_1 (.D(SRC), .Q(SRC_r), .clk(CLK), .clr(RST));  // open: en
  Register #(.width(32)) register_2 (.D(PC_1), .Q(PC_1_r), .clk(CLK), .clr(RST));  // open: en
  Register #(.width(1)) register_3 (.D(multiplexer_1_out), .Q(PCSrc_r), .clk(CLK), .clr(RST));  // open: en
  Register #(.width(32)) register_4 (.D(multiplexer_2_out), .Q(\立即数_r ), .clk(CLK), .clr(RST));  // open: en
  Register #(.width(32)) register_5 (.D(multiplexer_3_out), .Q(Instruction_r), .clk(CLK), .clr(RST));  // open: en
  Register #(.width(5)) register_6 (.D(multiplexer_4_out), .Q(W__r), .clk(CLK), .clr(RST));  // open: en
  Register #(.width(32)) register_7 (.D(multiplexer_5_out), .Q(ALU_X_r), .clk(CLK), .clr(RST));  // open: en
  Register #(.width(32)) register_8 (.D(multiplexer_6_out), .Q(ALU_Y_r), .clk(CLK), .clr(RST));  // open: en
  Register #(.width(32)) register_9 (.D(multiplexer_7_out), .Q(MemData_r), .clk(CLK), .clr(RST));  // open: en
  Register #(.width(4)) register_10 (.D(multiplexer_8_out), .Q(ALUOp_r), .clk(CLK), .clr(RST));  // open: en
  Register #(.width(1)) register_11 (.D(multiplexer_9_out), .Q(MemWrite_r), .clk(CLK), .clr(RST));  // open: en
  Register #(.width(1)) register_12 (.D(multiplexer_10_out), .Q(MemtoReg_r), .clk(CLK), .clr(RST));  // open: en
  Register #(.width(1)) register_13 (.D(multiplexer_11_out), .Q(RegWrite_r), .clk(CLK), .clr(RST));  // open: en
  Register #(.width(1)) register_14 (.D(multiplexer_12_out), .Q(Jump_r), .clk(CLK), .clr(RST));  // open: en

  // Notes on the sheet:
  //   注：这里使用了下拉电阻，如果清空信号不连接（即蓝色线），则复用器选择信号默认输入为0
endmodule
