// Logisim project _regfile参考设计.circ as structural Verilog: 2 circuits, main circuit main
module main (
  input  [4:0] Reg1_num,
  input  [4:0] Reg2,
  input  [4:0] Write_Reg_num,
  input  [31:0] Din,
  input  Write_Enable,
  input  Clock,
  output [31:0] Reg1,
  output [31:0] s0_Value,
  output [31:0] s1_Value,
  output [31:0] s2_Value,
  output [31:0] ra_Value,
  output [31:0] Reg2_2
);

  wire and_1_out, and_2_out, and_3_out, and_4_out, and_5_out, and_6_out, and_7_out, and_8_out, and_9_out,
       and_10_out, and_11_out, and_12_out, and_13_out, and_14_out, and_15_out, and_16_out, and_17_out,
       and_18_out, and_19_out, and_20_out, and_21_out, and_22_out, and_23_out, and_24_out, and_25_out,
       and_26_out, and_27_out, and_28_out, and_29_out, and_30_out, and_31_out, reg0_write, reg1_write,
       reg2_write, reg3_write, reg4_write, reg5_write, reg6_write, reg7_write, reg8_write, reg9_write,
       reg10_write, reg11_write, reg12_write, reg13_write, reg14_write, reg15_write, reg16_write,
       reg17_write, reg18_write, reg19_write, reg20_write, reg21_write, reg22_write, reg23_write,
       reg24_write, reg25_write, reg26_write, reg27_write, reg28_write, reg29_write, reg30_write, reg31_write;
  wire [31:0] reg1_out, reg2_out, reg3_out, reg4_out, reg5_out, reg6_out, reg7_out, reg8_out, reg9_out,
       reg10_out, reg11_out, reg12_out, reg13_out, reg14_out, reg15_out, reg19_out, reg20_out, reg21_out,
       reg22_out, reg23_out, reg24_out, reg25_out, reg26_out, reg27_out, reg28_out, reg29_out, reg30_out;

  Demultiplexer #(.select(5), .enable("false")) demultiplexer_1 (
    .out0(reg0_write), .out1(reg1_write), .out2(reg2_write), .out3(reg3_write), .out4(reg4_write),
    .out5(reg5_write), .out6(reg6_write), .out7(reg7_write), .out8(reg8_write), .out9(reg9_write),
    .out10(reg10_write), .out11(reg11_write), .out12(reg12_write), .out13(reg13_write), .out14(reg14_write),
    .out15(reg15_write), .out16(reg16_write), .out17(reg17_write), .out18(reg18_write), .out19(reg19_write),
    .out20(reg20_write), .out21(reg21_write), .out22(reg22_write), .out23(reg23_write), .out24(reg24_write),
    .out25(reg25_write), .out26(reg26_write), .out27(reg27_write), .out28(reg28_write), .out29(reg29_write),
    .out30(reg30_write), .out31(reg31_write), .in(1'b1), .sel(Write_Reg_num));
  and and_1 (and_1_out, reg1_write, Write_Enable);
  and and_2 (and_2_out, reg2_write, Write_Enable);
  and and_3 (and_3_out, reg3_write, Write_Enable);
  and and_4 (and_4_out, reg4_write, Write_Enable);
  and and_5 (and_5_out, reg5_write, Write_Enable);
  and and_6 (and_6_out, reg6_write, Write_Enable);
  and and_7 (and_7_out, reg7_write, Write_Enable);
  Register #(.width(32)) register_1 (.D(Din), .en(and_1_out), .Q(reg1_out), .clk(Clock));  // open: clr
  Register #(.width(32)) register_2 (.D(Din), .en(and_2_out), .Q(reg2_out), .clk(Clock));  // open: clr
  Register #(.width(32)) register_3 (.D(Din), .en(and_3_out), .Q(reg3_out), .clk(Clock));  // open: clr
  Register #(.width(32)) register_4 (.D(Din), .en(and_4_out), .Q(reg4_out), .clk(Clock));  // open: clr
  Register #(.width(32)) register_5 (.D(Din), .en(and_5_out), .Q(reg5_out), .clk(Clock));  // open: clr
  Register #(.width(32)) register_6 (.D(Din), .en(and_6_out), .Q(reg6_out), .clk(Clock));  // open: clr
  Register #(.width(32)) register_7 (.D(Din), .en(and_7_out), .Q(reg7_out), .clk(Clock));  // open: clr
  Register #(.width(32)) register_8 (.D(Din), .en(and_8_out), .Q(reg8_out), .clk(Clock));  // open: clr
  and and_8 (and_8_out, reg8_write, Write_Enable);
  Register #(.width(32)) register_9 (.D(Din), .en(and_9_out), .Q(reg9_out), .clk(Clock));  // open: clr
  and and_9 (and_9_out, reg9_write, Write_Enable);
  Register #(.width(32)) register_10 (.D(Din), .en(and_10_out), .Q(reg10_out), .clk(Clock));  // open: clr
  and and_10 (and_10_out, reg10_write, Write_Enable);
  Register #(.width(32)) register_11 (.D(Din), .en(and_11_out), .Q(reg11_out), .clk(Clock));  // open: clr
  and and_11 (and_11_out, reg11_write, Write_Enable);
  Register #(.width(32)) register_12 (.D(Din), .en(and_12_out), .Q(reg12_out), .clk(Clock));  // open: clr
  and and_12 (and_12_out, reg12_write, Write_Enable);
  Register #(.width(32)) register_13 (.D(Din), .en(and_13_out), .Q(reg13_out), .clk(Clock));  // open: clr
  and and_13 (and_13_out, reg13_write, Write_Enable);
  Register #(.width(32)) register_14 (.D(Din), .en(and_14_out), .Q(reg14_out), .clk(Clock));  // open: clr
  and and_14 (and_14_out, reg14_write, Write_Enable);
  Register #(.width(32)) register_15 (.D(Din), .en(and_15_out), .Q(reg15_out), .clk(Clock));  // open: clr
  and and_15 (and_15_out, reg15_write, Write_Enable);
  and and_16 (and_16_out, reg16_write, Write_Enable);
  and and_17 (and_17_out, reg17_write, Write_Enable);
  and and_18 (and_18_out, reg18_write, Write_Enable);
  and and_19 (and_19_out, reg19_write, Write_Enable);
  and and_20 (and_20_out, reg20_write, Write_Enable);
  and and_21 (and_21_out, reg21_write, Write_Enable);
  and and_22 (and_22_out, reg22_write, Write_Enable);
  and and_23 (and_23_out, reg23_write, Write_Enable);
  Register #(.width(32)) register_16 (.D(Din), .en(and_16_out), .Q(s0_Value), .clk(Clock));  // open: clr
  Register #(.width(32)) register_17 (.D(Din), .en(and_17_out), .Q(s1_Value), .clk(Clock));  // open: clr
  Register #(.width(32)) register_18 (.D(Din), .en(and_18_out), .Q(s2_Value), .clk(Clock));  // open: clr
  Register #(.width(32)) register_19 (.D(Din), .en(and_19_out), .Q(reg19_out), .clk(Clock));  // open: clr
  Register #(.width(32)) register_20 (.D(Din), .en(and_20_out), .Q(reg20_out), .clk(Clock));  // open: clr
  Register #(.width(32)) register_21 (.D(Din), .en(and_21_out), .Q(reg21_out), .clk(Clock));  // open: clr
  Register #(.width(32)) register_22 (.D(Din), .en(and_22_out), .Q(reg22_out), .clk(Clock));  // open: clr
  Register #(.width(32)) register_23 (.D(Din), .en(and_23_out), .Q(reg23_out), .clk(Clock));  // open: clr
  Register #(.width(32)) register_24 (.D(Din), .en(and_24_out), .Q(reg24_out), .clk(Clock));  // open: clr
  and and_24 (and_24_out, reg24_write, Write_Enable);
  Register #(.width(32)) register_25 (.D(Din), .en(and_25_out), .Q(reg25_out), .clk(Clock));  // open: clr
  and and_25 (and_25_out, reg25_write, Write_Enable);
  Register #(.width(32)) register_26 (.D(Din), .en(and_26_out), .Q(reg26_out), .clk(Clock));  // open: clr
  and and_26 (and_26_out, reg26_write, Write_Enable);
  Register #(.width(32)) register_27 (.D(Din), .en(and_27_out), .Q(reg27_out), .clk(Clock));  // open: clr
  and and_27 (and_27_out, reg27_write, Write_Enable);
  Register #(.width(32)) register_28 (.D(Din), .en(and_28_out), .Q(reg28_out), .clk(Clock));  // open: clr
  and and_28 (and_28_out, reg28_write, Write_Enable);
  Register #(.width(32)) register_29 (.D(Din), .en(and_29_out), .Q(reg29_out), .clk(Clock));  // open: clr
  and and_29 (and_29_out, reg29_write, Write_Enable);
  Register #(.width(32)) register_30 (.D(Din), .en(and_30_out), .Q(reg30_out), .clk(Clock));  // open: clr
  and and_30 (and_30_out, reg30_write, Write_Enable);
  Register #(.width(32)) register_31 (.D(Din), .en(and_31_out), .Q(ra_Value), .clk(Clock));  // open: clr
  and and_31 (and_31_out, reg31_write, Write_Enable);
  Multiplexer #(.select(5), .width(32), .enable("false")) multiplexer_1 (
    .in0({32{1'b0}}), .in1(reg1_out), .in2(reg2_out), .in3(reg3_out), .in4(reg4_out), .in5(reg5_out),
    .in6(reg6_out), .in7(reg7_out), .in8(reg8_out), .in9(reg9_out), .in10(reg10_out), .in11(reg11_out),
    .in12(reg12_out), .in13(reg13_out), .in14(reg14_out), .in15(reg15_out), .in16(s0_Value), .in17(s1_Value),
    .in18(s2_Value), .in19(reg19_out), .in20(reg20_out), .in21(reg21_out), .in22(reg22_out),
    .in23(reg23_out), .in24(reg24_out), .in25(reg25_out), .in26(reg26_out), .in27(reg27_out),
    .in28(reg28_out), .in29(reg29_out), .in30(reg30_out), .in31(ra_Value), .out(Reg1), .sel(Reg1_num));
  Multiplexer #(.select(5), .width(32), .enable("false")) multiplexer_2 (
    .in0({32{1'b0}}), .in1(reg1_out), .in2(reg2_out), .in3(reg3_out), .in4(reg4_out), .in5(reg5_out),
    .in6(reg6_out), .in7(reg7_out), .in8(reg8_out), .in9(reg9_out), .in10(reg10_out), .in11(reg11_out),
    .in12(reg12_out), .in13(reg13_out), .in14(reg14_out), .in15(reg15_out), .in16(s0_Value), .in17(s1_Value),
    .in18(s2_Value), .in19(reg19_out), .in20(reg20_out), .in21(reg21_out), .in22(reg22_out),
    .in23(reg23_out), .in24(reg24_out), .in25(reg25_out), .in26(reg26_out), .in27(reg27_out),
    .in28(reg28_out), .in29(reg29_out), .in30(reg30_out), .in31(ra_Value), .out(Reg2_2), .sel(Reg2));
  // NOT_Gate not_1 is placed but not wired

  // Other names for the same wires on the sheet: clk = Clock; reg2_num[4:0] = Reg2; reg2_t[31:0] = Reg2_2;
  //   reg16_out[31:0] = s0_Value; s0[31:0] = s0_Value; reg17_out[31:0] = s1_Value; s1[31:0] = s1_Value;
  //   reg18_out[31:0] = s2_Value; s2[31:0] = s2_Value; ra[31:0] = ra_Value; reg31_out[31:0] = ra_Value;
  //   WE = Write_Enable; write_data[31:0] = Din

  // Notes on the sheet:
  //   输入引脚
  //   输出引脚
  //   Debug引脚，便于观测寄存器值
  //   请勿修改引脚以及封装，直接使用隧道连接电路
  //   此设计为参考设计
endmodule

module test (
);

  wire undriven;

  main main_1 (.Clock(undriven));  // open: Reg1_num, Reg2, Write_Reg_num, Din, Write_Enable, Reg1, Reg2_2, s0_Value, s1_Value, s2_Value, ra_Value
endmodule
